# Fritzing sketch blink (saved by Fritzing 0.8.7b)
breadboards: 1

parts:
  Part1 = Arduino Uno (Rev3)
  LED = LED - 5mm [color="Red (633nm)" package="5 mm [THT]"]
  Resistor = Resistor [tolerance=±5% resistance=220 package=THT]

nets:
  N1: Part1.D13/SCK, Resistor.Pin_1
  N2: Part1.GND, LED.cathode
  N3: LED.anode, Resistor.Pin_0

notes:
  Examples -> 01. Basics -> Blink
  http://arduino.cc/en/tutorial/blink
