# Fritzing sketch button (saved by Fritzing 0.8.7b)
breadboards: 1

parts:
  Part1 = Arduino Uno (Rev3)
  LED = LED - 5mm [color="Red (633nm)" package="5 mm [THT]"]
  Resistor = Resistor [tolerance=±5% resistance=10k package=THT]
  Switch = Pushbutton [package="[THT]"]
  Resistor_2 = Resistor [tolerance=±5% resistance=220 package=THT]

nets:
  N1: Part1.D13/SCK, Resistor_2.Pin_0
  N2: Part1.GND, LED.cathode, Resistor.Pin_1
  N3: Part1.D2, Resistor.Pin_0, Switch.Pin_1, Switch.Pin_2
  N4: Part1.5V, Switch.Pin_3, Switch.Pin_4
  N5: LED.anode, Resistor_2.Pin_1

notes:
  Examples -> 02. Digital -> Button
  http://www.arduino.cc/en/Tutorial/Button
