# Fritzing sketch four_digit (saved by Fritzing 0.8.7b)
breadboards: 1

parts:
  Part1 = Arduino Uno (Rev3)
  R1 = Resistor [tolerance=±5% resistance=220 package=THT]
  R2 = Resistor [tolerance=±5% resistance=220 package=THT]
  R3 = Resistor [tolerance=±5% resistance=220 package=THT]
  R4 = Resistor [tolerance=±5% resistance=220 package=THT]
  R5 = Resistor [tolerance=±5% resistance=220 package=THT]
  R6 = Resistor [tolerance=±5% resistance=220 package=THT]
  R7 = Resistor [tolerance=±5% resistance=220 package=THT]
  R8 = Resistor [tolerance=±5% resistance=220 package=THT]
  U1 = 7-SEGMENT-4DIGIT [package=7-segment-4digit-5641]

nets:
  N1: Part1.D8, R8.Pin_0
  N2: Part1.D9_PWM, R7.Pin_0
  N3: Part1.D10_PWM/SS, R6.Pin_0
  N4: Part1.D11_PWM/MOSI, R5.Pin_0
  N5: Part1.D12/MISO, R4.Pin_0
  N6: Part1.D13/SCK, U1.DIG4
  N7: Part1.D2, U1.DIG1
  N8: Part1.D3_PWM, R1.Pin_0
  N9: Part1.D4, R2.Pin_0
  N10: Part1.D5_PWM, U1.DIG2
  N11: Part1.D6_PWM, U1.DIG3
  N12: Part1.D7, R3.Pin_0
  N13: R1.Pin_1, U1.A
  N14: R2.Pin_1, U1.F
  N15: R3.Pin_1, U1.B
  N16: R4.Pin_1, U1.G
  N17: R5.Pin_1, U1.C
  N18: R6.Pin_1, U1.DP
  N19: R7.Pin_1, U1.D
  N20: R8.Pin_1, U1.E

notes:
  http://learn.parallax.com/4-digit-7-segment-led-display-arduino-demo

custom parts:
  7-SEGMENT-4DIGIT: if you need make parts, send me e-mail and write. Price 1 part=0.9 WMZ (http://www.wmtransfer.com/) ~ 0.9 Euro
