# Fritzing sketch knight_rider (saved by Fritzing 0.8.7b)
breadboards: 1

parts:
  Part1 = Arduino Uno (Rev3)
  Resistor = Resistor [tolerance=±5% resistance=220 package=THT]
  Resistor1 = Resistor [tolerance=±5% resistance=220 package=THT]
  Resistor2 = Resistor [tolerance=±5% resistance=220 package=THT]
  Resistor3 = Resistor [tolerance=±5% resistance=220 package=THT]
  Resistor4 = Resistor [tolerance=±5% resistance=220 package=THT]
  Resistor5 = Resistor [tolerance=±5% resistance=220 package=THT]
  LED1 = LED - 5mm [color="Red (633nm)" package="5 mm [THT]"]
  LED2 = LED - 5mm [color="Red (633nm)" package="5 mm [THT]"]
  LED3 = LED - 5mm [color="Green (560nm)" package="5 mm [THT]"]
  LED4 = LED - 5mm [color="Green (560nm)" package="5 mm [THT]"]
  LED5 = LED - 5mm [color="Yellow (585nm)" package="5 mm [THT]"]
  LED6 = LED - 5mm [color="Yellow (585nm)" package="5 mm [THT]"]

nets:
  N1: Part1.GND, LED1.cathode, LED2.cathode, LED3.cathode, LED4.cathode, LED5.cathode, LED6.cathode
  N2: Part1.D2, Resistor.Pin_1
  N3: Part1.D3_PWM, Resistor1.Pin_1
  N4: Part1.D4, Resistor2.Pin_1
  N5: Part1.D5_PWM, Resistor3.Pin_1
  N6: Part1.D6_PWM, Resistor4.Pin_1
  N7: Part1.D7, Resistor5.Pin_1
  N8: Resistor.Pin_0, LED1.anode
  N9: Resistor1.Pin_0, LED2.anode
  N10: Resistor2.Pin_0, LED3.anode
  N11: Resistor3.Pin_0, LED4.anode
  N12: Resistor4.Pin_0, LED5.anode
  N13: Resistor5.Pin_0, LED6.anode

notes:
  Examples -> 05. Control -> Arrays
  http://arduino.cc/en/Tutorial/Array
