# Fritzing sketch light_detector (saved by Fritzing 0.8.7b)
breadboards: 1

parts:
  Part1 = Arduino Uno (Rev3)
  Light_detecting_diode = Photocell (LDR) [package=THT]
  R2 = Resistor [tolerance=±5% resistance=10k package=THT]
  R3 = Resistor [tolerance=±5% resistance=220 package=THT]
  LED1 = LED - 5mm [color="Red (633nm)" package="5 mm [THT]"]

nets:
  N1: Part1.A0, Light_detecting_diode.pin_0, R2.Pin_0
  N2: Part1.D13/SCK, R3.Pin_0
  N3: Part1.GND, R2.Pin_1, LED1.cathode
  N4: Part1.5V, Light_detecting_diode.pin_1
  N5: R3.Pin_1, LED1.anode

notes:
  http://playground.arduino.cc/Learning/PhotoResistor
