# Fritzing sketch magbot_budget (saved by Fritzing 0.8.7b)
breadboards: 1

parts:
  Part1 = Arduino Nano (Rev3.0)
  IC1 = L293D [package=THT]
  BATT2 = 4xAA Switchable Battery Pack w/Bare Wire
  Motor_A2 = DC Motor
  Motor_B2 = DC Motor
  Ping_Sensor3 = SRF05 Ultrasonic Rangefinder

nets:
  GND: Part1.GND, IC1.0V, BATT2.NEG, Ping_Sensor3.GND
  N1: Part1.D4, Ping_Sensor3.Echo
  N2: Part1.D5, IC1.Enable_1
  N3: Part1.D6, IC1.Enable_2
  N4: Part1.D7, Ping_Sensor3.Trig
  N5: Part1.D8, IC1.In_1
  N6: Part1.D12/MISO, IC1.In_2
  5V: Part1.5V, IC1.+V, Ping_Sensor3.VCC
  N7: Part1.A7, IC1.In_4
  N8: Part1.A6, IC1.In_3
  N9: IC1.Out_1_(_Controlled_by_Enable_1_), Motor_B2.pin_2
  N10: IC1.Out_2_(_Controlled_by_Enable_1_), Motor_B2.pin_1
  N11: IC1.+Vmotor, BATT2.POS
  N12: IC1.Out_3_(_Controlled_by_Enable_2_), Motor_A2.pin_2
  N13: IC1.Out_4_(_Controlled_by_Enable_2_), Motor_A2.pin_1

custom parts:
  4xAA Switchable Battery Pack w/Bare Wire: 4xAA Switchable Battery Pack with Bare Wire connection
