# Fritzing sketch matrix (saved by Fritzing 0.8.7b)
breadboards: 1

parts:
  Part1 = Arduino Uno (Rev3)
  Disp3 = LBT2088AH [part_number=LBT2088AH]
  Resistor8 = Resistor [tolerance=±5% resistance=220 package=THT]
  Resistor9 = Resistor [tolerance=±5% resistance=220 package=THT]
  Resistor10 = Resistor [tolerance=±5% resistance=220 package=THT]
  Resistor11 = Resistor [tolerance=±5% resistance=220 package=THT]
  Resistor12 = Resistor [tolerance=±5% resistance=220 package=THT]
  Resistor13 = Resistor [tolerance=±5% resistance=220 package=THT]
  Resistor14 = Resistor [tolerance=±5% resistance=220 package=THT]
  Resistor15 = Resistor [tolerance=±5% resistance=220 package=THT]

nets:
  N1: Part1.A0, Disp3.pin_8
  N2: Part1.A1, Disp3.pin_7
  N3: Part1.A2, Resistor13.Pin_0
  N4: Part1.A3, Disp3.pin_5
  N5: Part1.D8, Resistor8.Pin_0
  N6: Part1.D9_PWM, Disp3.pin_9
  N7: Part1.D10_PWM/SS, Disp3.pin1
  N8: Part1.D11_PWM/MOSI, Disp3.pin2
  N9: Part1.D12/MISO, Resistor10.Pin_0
  N10: Part1.D13/SCK, Resistor9.Pin_0
  N11: Part1.D2, Resistor15.Pin_0
  N12: Part1.D3_PWM, Resistor14.Pin_0
  N13: Part1.D4, Disp3.pin_14
  N14: Part1.D5_PWM, Resistor11.Pin_0
  N15: Part1.D6_PWM, Disp3.pin_12
  N16: Part1.D7, Resistor12.Pin_0
  N17: Disp3.pin_3, Resistor10.Pin_1
  N18: Disp3.pin_4, Resistor9.Pin_1
  N19: Disp3.pin_6, Resistor13.Pin_1
  N20: Disp3.pin_10, Resistor8.Pin_1
  N21: Disp3.pin_11, Resistor12.Pin_1
  N22: Disp3.pin_13, Resistor11.Pin_1
  N23: Disp3.pin_15, Resistor14.Pin_1
  N24: Disp3.pin_16, Resistor15.Pin_1

custom parts:
  LBT2088AH: LED Matrix Display 8x8 red 60.5mm
