# Fritzing sketch ping (saved by Fritzing 0.8.7b)
breadboards: 1

parts:
  Motor_Shield1 = Arduino Motor Shield (Rev3)
  Ping_Sensor2 = SRF05 Ultrasonic Rangefinder

nets:
  N1: Motor_Shield1.D4, Ping_Sensor2.Echo
  N2: Motor_Shield1.D7, Ping_Sensor2.Trig
  5V: Motor_Shield1.5V, Ping_Sensor2.VCC
  GND: Motor_Shield1.GND, Ping_Sensor2.GND
